# Fritzing sketch remote_control (saved by Fritzing 0.9.3b)

parts:
  Часть17 = NRF24L01+ Breakout Board  # not connected
  Часть18 = Arduino Uno (Rev3)
  Часть19 = Thumb Joystick
  Часть20 = Thumb Joystick
  U1 = SWITCH-SPST-2 [package=switch-spst-vertical]
  S1 = Round Pushbutton

nets:
  N1: Часть18.A0, Часть20.VERT
  N2: Часть18.A1, Часть19.VERT
  N3: Часть18.D8, S1.leg0
  GND: Часть18.GND, Часть19.GND, Часть20.GND
  N4: Часть18.D2, U1.O
  VCC: Часть18.5V, Часть19.VCC, Часть20.VCC, U1.P, S1.leg1

notes:
  PowerBank
  CE
  CSN
  MO
  MI
  IR0 VCC GND
  =====>
