# Fritzing sketch robot (saved by Fritzing 0.9.3b)

parts:
  Часть1 = Arduino Mega 2560 (Rev3)
  Часть3 = Arduino Motor Shield (Rev3)
  Часть4 = NRF24L01+ Breakout Board  # not connected
  M1 = DC Motor
  M2 = DC Motor
  Часть5 = ws2812b [package="smd 2812b"]
  Часть6 = ws2812b [package="smd 2812b"]
  Часть7 = ws2812b [package="smd 2812b"]
  Часть8 = ws2812b [package="smd 2812b"]
  Часть9 = ws2812b [package="smd 2812b"]
  VCC1 = Battery

nets:
  VSS: Часть1.GND, Часть3.GND, Часть5.VSS, Часть6.VSS, Часть7.VSS, Часть8.VSS, Часть9.VSS, VCC1.-
  VIN: Часть1.VIN, Часть3.VIN
  N1: Часть3.D8/BreakeB, Часть5.DIN
  N2: Часть3.B-, M2.pin_2
  N3: Часть3.B+, M2.pin_1
  N4: Часть3.A-, M1.pin_1
  N5: Часть3.A+, M1.pin_2
  N6: Часть3.VMOT, VCC1.+
  VDD: Часть3.5V, Часть5.VDD, Часть6.VDD, Часть7.VDD, Часть8.VDD, Часть9.VDD
  N7: Часть5.DOUT, Часть6.DIN
  N8: Часть6.DOUT, Часть7.DIN
  N9: Часть7.DOUT, Часть8.DIN
  N10: Часть8.DOUT, Часть9.DIN

notes:
  18650
  Pins for control motors in our motors shield is 4,5,6,7
  So, the pins are different from the shield shown in the figure !!!
  CE
  CSN
  MO
  MI
  IR0 VCC GND
